# Fritzing sketch Schematics (saved by Fritzing 1.0.7)
circuit board: 8.46667cm x 5.64444cm
breadboards: 1

parts:
  Part1 = Adafruit HUZZAH ESP8266 [part_number="Adafruit #2471"]
  RTC_connector = female pin header, 4 pins [form="♀ (female)"]
  DFRobot_DFPlayer_Mini1 = DFRobot DFPlayer Mini [part_number=DFR0299]
  Plr_rx = Resistor [tolerance=±5% resistance=1k package="2512 [SMD]"]
  Speaker_connector = female pin header, 2 pins [form="♀ (female)"]
  Pump_connector = female pin header, 2 pins [form="♀ (female)"]
  Q1 = npn-Powertransistor [package="TO220 [THT]"]
  R2 = Resistor [tolerance=±5% resistance=100 package="2512 [SMD]"]
  D1 = Rectifier Diode [part_number=1N4001 package="300 mil [THT]"]
  Button_connector = female pin header, 2 pins [form="♀ (female)"]
  R3 = Resistor [tolerance=±5% resistance=220 package="2512 [SMD]"]
  Pot_connector = female pin header, 3 pins [form="♀ (female)"]

nets:
  N1: Part1.ADC, Pot_connector.pin3
  N2: Part1.GPIO12, Plr_rx.Pin_0
  N3: Part1.GPIO13, DFRobot_DFPlayer_Mini1.TX
  N4: Part1.GND, RTC_connector.pin4, DFRobot_DFPlayer_Mini1.GND-1, DFRobot_DFPlayer_Mini1.GND-2, Q1.emitter, Button_connector.pin2, R3.Pin_1, Pot_connector.pin1
  3.3V: Part1.3.3V, RTC_connector.pin3, DFRobot_DFPlayer_Mini1.VCC, Pump_connector.pin1, D1.cathode, Pot_connector.pin2
  N5: Part1.GPIO2, R2.Pin_0
  N6: Part1.GPIO0, Button_connector.pin1
  N7: Part1.GPIO4, RTC_connector.pin2
  N8: Part1.GPIO5, RTC_connector.pin1
  N9: DFRobot_DFPlayer_Mini1.RX, Plr_rx.Pin_1
  N10: DFRobot_DFPlayer_Mini1.SPK_1, Speaker_connector.pin1
  N11: DFRobot_DFPlayer_Mini1.SPK_2, Speaker_connector.pin2
  N12: Pump_connector.pin2, Q1.collector, D1.anode
  N13: Q1.base, R2.Pin_1, R3.Pin_0
